// Logisim project GatesusingotherGates.circ as structural Verilog: 1 circuit, main circuit main
module main (
  input  in_1,
  input  in_2,
  input  in_3,
  input  in_4,
  input  in_5,
  input  in_6,
  input  in_7,
  input  in_8,
  input  in_9,
  input  in_10,
  input  in_11,
  input  in_12,
  output out_13,
  output out_14,
  output out_15,
  output out_16,
  output out_17,
  output out_18,
  output out_19
);

  wire nand_1_out, nand_2_out, nand_3_out, nand_5_out, nand_6_out, nor_1_out, nor_2_out, nor_3_out,
       nor_4_out, nor_5_out, nor_6_out, nor_8_out, nor_9_out, nor_10_out, nor_11_out, nor_13_out;

  nor nor_1 (nor_1_out, in_4, in_4);
  nor nor_2 (nor_2_out, in_5, in_5);
  nor nor_3 (nor_3_out, in_6, in_6);
  nor nor_4 (nor_4_out, in_7, in_7);
  nor nor_5 (nor_5_out, in_5, nor_1_out);
  nor nor_6 (nor_6_out, in_4, nor_2_out);
  nand nand_1 (nand_1_out, in_9, in_10);
  nand nand_2 (nand_2_out, in_11, in_11);
  nand nand_3 (nand_3_out, in_12, in_12);
  nor nor_7 (out_13, in_1, in_1);
  nor nor_8 (nor_8_out, in_2, in_2);
  nor nor_9 (nor_9_out, in_3, in_3);
  nor nor_10 (nor_10_out, in_7, nor_3_out);
  nor nor_11 (nor_11_out, in_6, nor_4_out);
  nor nor_12 (out_14, nor_8_out, nor_9_out);
  nor nor_13 (nor_13_out, nor_5_out, nor_6_out);
  nand nand_4 (out_17, in_8, in_8);
  nand nand_5 (nand_5_out, nand_2_out, in_12);
  nand nand_6 (nand_6_out, nand_3_out, in_11);
  nor nor_14 (out_16, nor_10_out, nor_11_out);
  nand nand_7 (out_18, nand_1_out, nand_1_out);
  nor nor_15 (out_15, nor_13_out, nor_13_out);
  nand nand_8 (out_19, nand_5_out, nand_6_out);

  // Notes on the sheet:
  //   Gates using NOR Gate
  //   Gates using NAND Gate
  //   NOT using NOR
  //   XNOR using NOR
  //   NOT using NAND
  //   XOR using NAND
  //   AND using NOR
  //   XOR using NOR
  //   AND using NAND
endmodule
